// Logisim project thing.circ as structural Verilog: 9 circuits, main circuit main
module main (
);

  wire button_1_out, button_2_out, button_3_out, CLK, cpu_1_int, cpu_1_iowen, devicetty_1_ttyclk,
       devicetty_1_ttyclr, devicetty_1_ttyen, keyboard_1_avail, MWEN, PWR, register_1_q, RST, undriven,
       undriven_2;
  wire [3:0] cpu_1_intaddr, cpu_1_intcode;
  wire [6:0] devicetty_1_ttyascii, keyboard_1_data;
  wire [15:0] cpu_1_ioaddr, cpu_1_iowrite, devicemanager_1_ior, DOUT0, DOUT1, DOUT2, MADDR, MIN, MW;
  wire [38:0] DIN0, DIN1, DIN2;

  Register #(.width(1)) register_1 (.D(PWR), .en(1'b1), .clk(CLK), .Q(register_1_q), .clr(RST));
  Clock clock_1 (.out(CLK));
  RAM #(.addrWidth(16), .dataWidth(16), .enables("line"), .\type ("nonvolatile")) ram_1 (
    .addr(MADDR), .we(MWEN), .clk(CLK), .din(MW), .dout(MIN));
  CPU cpu_1 (
    .RAMIN(MIN), .IOREAD(devicemanager_1_ior), .EN(register_1_q), .RST(RST), .CLK(CLK), .IOWEN(cpu_1_iowen),
    .IOADDR(cpu_1_ioaddr), .IOWRITE(cpu_1_iowrite), .RAMWEN(MWEN), .RAMWRITE(MW), .RAMADDR(MADDR),
    .INT(cpu_1_int), .INTADDR(cpu_1_intaddr), .INTCODE(cpu_1_intcode));
  Button button_1 (.out(button_1_out));
  DeviceManager devicemanager_1 (
    .IOW(cpu_1_iowrite), .INTCODE(cpu_1_intcode), .CLK(CLK), .R0(DOUT0), .R1(DOUT1), .R2(DOUT2),
    .IOADDR(cpu_1_ioaddr), .INT(cpu_1_int), .INTADDR(cpu_1_intaddr), .WEN(cpu_1_iowen), .D0(DIN0), .D1(DIN1),
    .D2(DIN2), .IOR(devicemanager_1_ior));  // open: R7, R8, R9, RA, RB, RC, RD, RE, RF, R3, R4, R5, R6, D7, D8, D9, DA, DB, DC, DD, DE, DF, D3, D4, D5, D6
  Button button_2 (.out(button_2_out));
  Button button_3 (.out(button_3_out));
  DevicePower devicepower_1 (
    .DIN(DIN0), .PWROFF(button_3_out), .MRST(button_2_out), .PWRON(button_1_out), .RST(RST), .PWR(PWR),
    .DOUT(DOUT0));
  TTY #(.trigger("falling")) tty_1 (
    .data(devicetty_1_ttyascii), .clk(devicetty_1_ttyclk), .we(devicetty_1_ttyen), .clr(devicetty_1_ttyclr));
  DeviceTTY devicetty_1 (
    .DIN(DIN1), .TTYCLK(devicetty_1_ttyclk), .TTYASCII(devicetty_1_ttyascii), .TTYEN(devicetty_1_ttyen),
    .TTYCLR(devicetty_1_ttyclr), .DOUT(DOUT1));
  Keyboard keyboard_1 (.clk(undriven), .clr(undriven_2), .avail(keyboard_1_avail), .data(keyboard_1_data));  // open: re
  DeviceKeyboard devicekeyboard_1 (
    .KEYCLK(undriven), .DIN(DIN2), .KEYRST(undriven_2), .KEYA(keyboard_1_avail), .KEYD(keyboard_1_data),
    .DOUT(DOUT2));
endmodule

module CPU (
  input  CLK,
  input  EN,
  input  RST,
  input  [15:0] RAMIN,
  input  [15:0] IOREAD,
  output [15:0] RAMADDR,
  output RAMWEN,
  output [15:0] RAMWRITE,
  output INT,
  output IOWEN,
  output [3:0] INTADDR,
  output [15:0] IOADDR,
  output [3:0] INTCODE,
  output [15:0] IOWRITE
);

  wire and_8_out, and_9_out, and_13_out, and_15_out, and_16_out, button_1_out, button_2_out, CLK_t,
       clock_1_out, I_ADDI, I_JMP, I_LUI, I_LW, I_MATH, I_SW, JMP, nand_1_out, not_1_out, or_1_out, or_3_out,
       or_5_out, or_7_out, or_8_out, or_9_out, REGW, RST_t, t_ff_1_q;
  wire [2:0] alu_1_neg, and_12_out, and_14_out, bit_extender_2_out, f0_q;
  wire [3:0] BA, INST, multiplexer_2_out, multiplexer_3_out;
  wire [15:0] adder_1_out, bit_extender_1_out, bit_extender_4_out, bit_extender_5_out, bit_extender_6_out,
       DIN, I0, I1, I2, IMM, multiplexer_1_out, multiplexer_4_out, multiplexer_7_out, multiplexer_8_out,
       multiplexer_9_out, multiplexer_10_out, PC, RA, RAMOUT, shifter_1_out, SINT;

  Clock clock_1 (.out(clock_1_out));
  T_Flip_Flop t_ff_1 (.T(1'b1), .clk(button_1_out), .Q(t_ff_1_q));  // open: Qn, reset, preset
  Button button_1 (.out(button_1_out));
  Button button_2 (.out(button_2_out));
  or or_1 (or_1_out, clock_1_out, CLK);
  or or_2 (RST_t, button_2_out, RST);
  and and_1 (I_LW, ~INST[0], ~INST[1], ~INST[2], INST[3]);  // AND_Gate
  and and_2 (I_SW, INST[0], ~INST[1], ~INST[2], INST[3]);  // AND_Gate
  and and_3 (I_ADDI, ~INST[0], INST[1], ~INST[2], INST[3]);  // AND_Gate
  and and_4 (I_LUI, INST[0], INST[1], ~INST[2], INST[3]);  // AND_Gate
  and and_5 (I_MATH, ~INST[0], ~INST[1], INST[2], INST[3]);  // AND_Gate
  and and_6 (INT, INST[0], ~INST[1], INST[2], INST[3]);  // AND_Gate
  and and_7 (I_JMP, ~INST[0], INST[1], INST[2], INST[3]);  // AND_Gate
  or or_3 (or_3_out, t_ff_1_q, EN);
  or or_4 (CLK_t, or_1_out, ~or_3_out);  // OR_Gate
  assign bit_extender_1_out = {{8{INTADDR[3]}}, {INTADDR, BA}};  // Bit_Extender bit_extender_1
  and and_8 (and_8_out, ~INTCODE[3], JMP, I_JMP);  // AND_Gate
  Adder #(.width(16)) adder_1 (.a(PC), .b(multiplexer_1_out), .out(adder_1_out));  // open: cin, cout
  Multiplexer #(.width(16)) multiplexer_1 (
    .in0(16'h1), .in1(bit_extender_1_out), .out(multiplexer_1_out), .sel(and_8_out));
  Multiplexer #(.width(4)) multiplexer_2 (.in0(BA), .in1(INTADDR), .out(multiplexer_2_out), .sel(I_ADDI));
  Multiplexer #(.width(4)) multiplexer_3 (.in0(INTCODE), .in1(INTADDR), .out(multiplexer_3_out), .sel(I_SW));
  RegFile regfile_1 (
    .D(DIN), .CLK(CLK_t), .RST(RST_t), .DSEL(INTADDR), .EN(REGW), .PCIN(adder_1_out),
    .ASEL(multiplexer_2_out), .BSEL(multiplexer_3_out), .PCOUT(PC), .A(RA), .B(IOWRITE));
  and and_9 (and_9_out, IOADDR[12], IOADDR[13], IOADDR[14], IOADDR[15]);
  and and_10 (IOWEN, and_9_out, I_SW);
  assign bit_extender_2_out = {{2{INST[3]}}, INST[3]};  // Bit_Extender bit_extender_2
  or or_5 (or_5_out, I_ADDI, I_LUI, I_LW, I_SW);
  and and_11 (RAMWEN, ~and_9_out, I_SW);  // AND_Gate
  assign and_12_out = INST[2:0] & ~bit_extender_2_out;  // AND_Gate and_12, 3 bits wide
  Multiplexer #(.width(16)) multiplexer_4 (.in0(IOWRITE), .in1(IMM), .out(multiplexer_4_out), .sel(or_5_out));
  not not_1 (not_1_out, INST[3]);
  ALU alu_1 (
    .A(RA), .B(multiplexer_4_out), .OP(and_12_out), .OUT(IOADDR), .NEG(alu_1_neg[0]), .ZERO(alu_1_neg[1]),
    .POS(alu_1_neg[2]));
  Register #(.width(3)) f0 (.D(alu_1_neg), .en(not_1_out), .clk(CLK_t), .Q(f0_q), .clr(RST_t));
  Multiplexer #(.width(16)) multiplexer_5 (.in0(IOADDR), .in1(PC), .out(RAMADDR), .sel(CLK_t));
  assign I2 = {{13{1'b0}}, f0_q};  // Bit_Extender bit_extender_3
  Multiplexer #(.width(16)) multiplexer_6 (.in0(RAMIN), .in1(IOREAD), .out(RAMOUT), .sel(and_13_out));
  and and_13 (and_13_out, and_9_out, ~CLK_t);  // AND_Gate
  nand nand_1 (nand_1_out, I_JMP, INTCODE[3]);
  assign and_14_out = INTCODE[2:0] & I2[2:0];  // AND_Gate and_14, 3 bits wide
  and and_15 (and_15_out, INST[2], nand_1_out);
  Register #(.trigger("falling"), .width(16)) register_1 (
    .D(RAMOUT), .en(1'b1), .clk(CLK_t), .Q({INTCODE, BA, INTADDR, INST}), .clr(RST_t));
  or or_6 (JMP, and_14_out[0], and_14_out[1], and_14_out[2]);
  or or_7 (or_7_out, I_SW, and_15_out);
  nand nand_2 (REGW, INST[3], or_7_out);
  MathU mathu_1 (.A(RA), .B(IOWRITE), .OP(INTADDR), .EN(I_MATH), .CLK(CLK_t), .RST(RST_t), .OUT0(I0), .OUT1(I1));
  assign bit_extender_4_out = {{8{BA[3]}}, {BA, INTCODE}};  // Bit_Extender bit_extender_4
  Shifter #(.width(16)) shifter_1 (.in(bit_extender_4_out), .\dist (4'b1000), .out(shifter_1_out));
  Multiplexer #(.width(16)) multiplexer_7 (.in0(IOADDR), .in1(RAMOUT), .out(multiplexer_7_out), .sel(I_LW));
  assign bit_extender_5_out = {{8{INTADDR[3]}}, {INTADDR, BA}};  // Bit_Extender bit_extender_5
  Multiplexer #(.width(16)) multiplexer_8 (
    .in0(bit_extender_5_out), .in1(multiplexer_9_out), .out(multiplexer_8_out), .sel(or_8_out));
  Multiplexer #(.width(16)) multiplexer_9 (
    .in0(bit_extender_4_out), .in1(shifter_1_out), .out(multiplexer_9_out), .sel(I_LUI));
  or or_8 (or_8_out, I_LUI, I_ADDI);
  Multiplexer #(.width(16)) multiplexer_10 (.in0(multiplexer_7_out), .in1(IMM), .out(multiplexer_10_out), .sel(I_LUI));
  or or_9 (or_9_out, I_LW, I_SW);
  assign bit_extender_6_out = {{12{INTCODE[3]}}, INTCODE};  // Bit_Extender bit_extender_6
  Multiplexer #(.width(16)) multiplexer_11 (.in0(multiplexer_10_out), .in1(SINT), .out(DIN), .sel(and_16_out));
  and and_16 (and_16_out, INTCODE[3], I_JMP);
  Multiplexer #(.width(16)) multiplexer_12 (
    .in0(multiplexer_8_out), .in1(bit_extender_6_out), .out(IMM), .sel(or_9_out));
  Multiplexer #(.select(3), .width(16)) multiplexer_13 (
    .in0(I0), .in1(I1), .in2(I2), .in3({16{1'b0}}), .in4({16{1'b0}}), .in5({16{1'b0}}), .in6({16{1'b0}}),
    .in7({16{1'b0}}), .out(SINT), .sel(INTCODE[2:0]));

  assign RAMWRITE = IOWRITE;

  // Other names for the same wires on the sheet: BB[3:0] = INTCODE; INST[15:4] = {INTCODE, BA, INTADDR};
  //   BD[3:0] = INTADDR; ALUOUT[15:0] = IOADDR; I_INT = INT; OPCODE[3:0] = INST; RB[15:0] = IOWRITE
endmodule

module RegFile (
  input  CLK,
  input  RST,
  input  [15:0] D,
  input  [15:0] PCIN,
  input  EN,
  input  [3:0] DSEL,
  input  [3:0] ASEL,
  input  [3:0] BSEL,
  output [15:0] A,
  output [15:0] B,
  output [15:0] PCOUT
);

  wire demultiplexer_1_out1, demultiplexer_1_out2, demultiplexer_1_out3, demultiplexer_1_out4,
       demultiplexer_1_out5, demultiplexer_1_out6, demultiplexer_1_out7, demultiplexer_1_out8,
       demultiplexer_1_out9, demultiplexer_1_out10, demultiplexer_1_out11, demultiplexer_1_out12,
       demultiplexer_1_out13, demultiplexer_1_out14, demultiplexer_1_out15;
  wire [15:0] multiplexer_1_out, O2, O3, O4, O5, O6, O7, O8, O9, OA, OB, OC, OD, OE, OF;

  Demultiplexer #(.select(4)) demultiplexer_1 (
    .out1(demultiplexer_1_out1), .out2(demultiplexer_1_out2), .out3(demultiplexer_1_out3),
    .out4(demultiplexer_1_out4), .out5(demultiplexer_1_out5), .out6(demultiplexer_1_out6),
    .out7(demultiplexer_1_out7), .out8(demultiplexer_1_out8), .out9(demultiplexer_1_out9),
    .out10(demultiplexer_1_out10), .out11(demultiplexer_1_out11), .out12(demultiplexer_1_out12),
    .out13(demultiplexer_1_out13), .out14(demultiplexer_1_out14), .out15(demultiplexer_1_out15), .in(EN),
    .sel(DSEL));  // open: out0
  Multiplexer #(.width(16)) multiplexer_1 (.in0(PCIN), .in1(D), .out(multiplexer_1_out), .sel(demultiplexer_1_out1));
  Register #(.width(16)) r8 (.D(D), .en(demultiplexer_1_out15), .Q(OF), .clk(CLK), .clr(RST));
  Register #(.width(16)) pc (.D(multiplexer_1_out), .en(1'b1), .Q(PCOUT), .clk(CLK), .clr(RST));
  Register #(.width(16)) r7 (.D(D), .en(demultiplexer_1_out14), .Q(OE), .clk(CLK), .clr(RST));
  Multiplexer #(.select(4), .width(16)) multiplexer_2 (
    .in0({16{1'b0}}), .in1(PCOUT), .in2(O2), .in3(O3), .in4(O4), .in5(O5), .in6(O6), .in7(O7), .in8(O8),
    .in9(O9), .in10(OA), .in11(OB), .in12(OC), .in13(OD), .in14(OE), .in15(OF), .out(A), .sel(ASEL));
  Register #(.width(16)) data (.D(D), .en(demultiplexer_1_out2), .Q(O2), .clk(CLK));  // open: clr
  Register #(.width(16)) r6 (.D(D), .en(demultiplexer_1_out13), .Q(OD), .clk(CLK), .clr(RST));
  Register #(.width(16)) code (.D(D), .en(demultiplexer_1_out3), .Q(O3), .clk(CLK), .clr(RST));
  Register #(.width(16)) r5 (.D(D), .en(demultiplexer_1_out12), .Q(OC), .clk(CLK), .clr(RST));
  Register #(.width(16)) sp (.D(D), .en(demultiplexer_1_out4), .Q(O4), .clk(CLK), .clr(RST));
  Register #(.width(16)) r4 (.D(D), .en(demultiplexer_1_out11), .Q(OB), .clk(CLK), .clr(RST));
  Register #(.width(16)) hp (.D(D), .en(demultiplexer_1_out5), .Q(O5), .clk(CLK), .clr(RST));
  Register #(.width(16)) r3 (.D(D), .en(demultiplexer_1_out10), .Q(OA), .clk(CLK), .clr(RST));
  Multiplexer #(.select(4), .width(16)) multiplexer_3 (
    .in0({16{1'b0}}), .in1(PCOUT), .in2(O2), .in3(O3), .in4(O4), .in5(O5), .in6(O6), .in7(O7), .in8(O8),
    .in9(O9), .in10(OA), .in11(OB), .in12(OC), .in13(OD), .in14(OE), .in15(OF), .out(B), .sel(BSEL));
  Register #(.width(16)) bp (.D(D), .en(demultiplexer_1_out6), .Q(O6), .clk(CLK), .clr(RST));
  Register #(.width(16)) r2 (.D(D), .en(demultiplexer_1_out9), .Q(O9), .clk(CLK), .clr(RST));
  Register #(.width(16)) r0 (.D(D), .en(demultiplexer_1_out7), .Q(O7), .clk(CLK), .clr(RST));
  Register #(.width(16)) r1 (.D(D), .en(demultiplexer_1_out8), .Q(O8), .clk(CLK), .clr(RST));

  // Other names for the same wires on the sheet: O1[15:0] = PCOUT
endmodule

module ALU (
  input  [2:0] OP,
  input  [15:0] A,
  input  [15:0] B,
  output ZERO,
  output POS,
  output NEG,
  output [15:0] OUT
);

  wire [15:0] adder_1_out, and_1_out, bit_extender_1_out, bit_extender_2_out, multiplexer_1_out,
       multiplexer_2_out, or_1_out, shifter_1_out, shifter_2_out, xor_1_out, xor_2_out, xor_3_out;

  assign bit_extender_1_out = {{15{OP[0]}}, OP[0]};  // Bit_Extender bit_extender_1
  assign xor_1_out = B ^ bit_extender_1_out;  // XOR_Gate xor_1, 16 bits wide
  assign bit_extender_2_out = {{15{OP[0]}}, OP[0]};  // Bit_Extender bit_extender_2
  Adder #(.width(16)) adder_1 (.a(A), .b(xor_1_out), .out(adder_1_out), .cin(OP[0]));  // open: cout
  Shifter #(.width(16)) shifter_1 (.in(A), .\dist (B[3:0]), .out(shifter_1_out));
  Shifter #(.shift("lr"), .width(16)) shifter_2 (.in(A), .\dist (B[3:0]), .out(shifter_2_out));
  assign and_1_out = A & B;  // AND_Gate and_1, 16 bits wide
  assign or_1_out = A | B;  // OR_Gate or_1, 16 bits wide
  assign xor_2_out = A ^ B;  // XOR_Gate xor_2, 16 bits wide
  Multiplexer #(.width(16)) multiplexer_1 (
    .in0(shifter_1_out), .in1(shifter_2_out), .out(multiplexer_1_out), .sel(OP[0]));
  assign xor_3_out = and_1_out ^ bit_extender_2_out;  // XOR_Gate xor_3, 16 bits wide
  Multiplexer #(.width(16)) multiplexer_2 (.in0(or_1_out), .in1(xor_2_out), .out(multiplexer_2_out), .sel(OP[0]));
  Multiplexer #(.select(2), .width(16)) multiplexer_3 (
    .in0(adder_1_out), .in1(multiplexer_1_out), .in2(xor_3_out), .in3(multiplexer_2_out),
    .out({NEG, OUT[14:0]}), .sel(OP[2:1]));
  nor nor_1 (ZERO, OUT[0], OUT[1], OUT[2], OUT[3], OUT[4], OUT[5], OUT[6], OUT[7], OUT[8], OUT[9], OUT[10], OUT[11], OUT[12], OUT[13], OUT[14], NEG);
  nor nor_2 (POS, ZERO, NEG);

  assign OUT[15] = NEG;

  // Other names for the same wires on the sheet: OP12[1:0] = OP[2:1]
endmodule

module MathU (
  input  [3:0] OP,
  input  EN,
  input  RST,
  input  CLK,
  input  [15:0] A,
  input  [15:0] B,
  output [15:0] OUT0,
  output [15:0] OUT1
);

  wire [15:0] divider_1_out, divider_1_rem, multiplier_1_cout, multiplier_1_out;
  wire [31:0] multiplexer_1_out;

  Multiplier #(.width(16)) multiplier_1 (.a(A), .b(B), .out(multiplier_1_out), .cout(multiplier_1_cout));  // open: cin
  Divider #(.width(16)) divider_1 (.a(A), .b(B), .out(divider_1_out), .rem(divider_1_rem));  // open: upper
  Multiplexer #(.width(32)) multiplexer_1 (
    .in0({multiplier_1_cout, multiplier_1_out}), .in1({divider_1_rem, divider_1_out}),
    .out(multiplexer_1_out), .sel(OP[0]));
  Register #(.width(16)) m0 (.D(multiplexer_1_out[15:0]), .en(EN), .clk(CLK), .Q(OUT0), .clr(RST));
  Register #(.width(16)) m1 (.D(multiplexer_1_out[31:16]), .en(EN), .clk(CLK), .Q(OUT1), .clr(RST));
endmodule

module DeviceManager (
  input  [15:0] IOADDR,
  input  [15:0] IOW,
  input  [3:0] INTCODE,
  input  CLK,
  input  WEN,
  input  INT,
  input  [3:0] INTADDR,
  input  [15:0] R0,
  input  [15:0] R1,
  input  [15:0] R2,
  input  [15:0] R3,
  input  [15:0] R4,
  input  [15:0] R5,
  input  [15:0] R6,
  input  [15:0] R7,
  input  [15:0] R8,
  input  [15:0] R9,
  input  [15:0] RA,
  input  [15:0] RB,
  input  [15:0] RC,
  input  [15:0] RD,
  input  [15:0] RE,
  input  [15:0] RF,
  output [38:0] D0,
  output [38:0] D1,
  output [38:0] D2,
  output [38:0] D3,
  output [38:0] D4,
  output [15:0] IOR,
  output [38:0] D5,
  output [38:0] D6,
  output [38:0] D7,
  output [38:0] D8,
  output [38:0] D9,
  output [38:0] DA,
  output [38:0] DB,
  output [38:0] DC,
  output [38:0] DD,
  output [38:0] DE,
  output [38:0] DF
);

  Multiplexer #(.select(4), .width(16)) multiplexer_1 (
    .in0(R0), .in1(R1), .in2(R2), .in3(R3), .in4(R4), .in5(R5), .in6(R6), .in7(R7), .in8(R8), .in9(R9),
    .in10(RA), .in11(RB), .in12(RC), .in13(RD), .in14(RE), .in15(RF), .out(IOR), .sel(IOADDR[11:8]));
  Demultiplexer #(.select(4)) demultiplexer_1 (
    .out0(D0[37]), .out1(D1[37]), .out2(D2[37]), .out3(D3[37]), .out4(D4[37]), .out5(D5[37]), .out6(D6[37]),
    .out7(D7[37]), .out8(D8[37]), .out9(D9[37]), .out10(DA[37]), .out11(DB[37]), .out12(DC[37]),
    .out13(DD[37]), .out14(DE[37]), .out15(DF[37]), .in(INT), .sel(INTADDR));
  Demultiplexer #(.select(4)) demultiplexer_2 (
    .out0(D0[0]), .out1(D1[0]), .out2(D2[0]), .out3(D3[0]), .out4(D4[0]), .out5(D5[0]), .out6(D6[0]),
    .out7(D7[0]), .out8(D8[0]), .out9(D9[0]), .out10(DA[0]), .out11(DB[0]), .out12(DC[0]), .out13(DD[0]),
    .out14(DE[0]), .out15(DF[0]), .in(WEN), .sel(IOADDR[11:8]));

  assign {D0[38], D0[36:1]} = {CLK, INTCODE, IOW, IOADDR};
  assign {D1[38], D1[36:1]} = {CLK, INTCODE, IOW, IOADDR};
  assign {D2[38], D2[36:1]} = {CLK, INTCODE, IOW, IOADDR};
  assign {D3[38], D3[36:1]} = {CLK, INTCODE, IOW, IOADDR};
  assign {D4[38], D4[36:1]} = {CLK, INTCODE, IOW, IOADDR};
  assign {D5[38], D5[36:1]} = {CLK, INTCODE, IOW, IOADDR};
  assign {D6[38], D6[36:1]} = {CLK, INTCODE, IOW, IOADDR};
  assign {D7[38], D7[36:1]} = {CLK, INTCODE, IOW, IOADDR};
  assign {D8[38], D8[36:1]} = {CLK, INTCODE, IOW, IOADDR};
  assign {D9[38], D9[36:1]} = {CLK, INTCODE, IOW, IOADDR};
  assign {DA[38], DA[36:1]} = {CLK, INTCODE, IOW, IOADDR};
  assign {DB[38], DB[36:1]} = {CLK, INTCODE, IOW, IOADDR};
  assign {DC[38], DC[36:1]} = {CLK, INTCODE, IOW, IOADDR};
  assign {DD[38], DD[36:1]} = {CLK, INTCODE, IOW, IOADDR};
  assign {DE[38], DE[36:1]} = {CLK, INTCODE, IOW, IOADDR};
  assign {DF[38], DF[36:1]} = {CLK, INTCODE, IOW, IOADDR};
endmodule

module DevicePower (
  input  [38:0] DIN,
  input  PWRON,
  input  PWROFF,
  input  MRST,
  output PWR,
  output [15:0] DOUT,
  output RST
);

  wire and_2_out, and_3_out, INT, or_1_out;

  and and_1 (INT, DIN[37], DIN[38]);
  and and_2 (and_2_out, ~DIN[33], ~DIN[34], ~DIN[35], ~DIN[36], INT);  // AND_Gate
  and and_3 (and_3_out, DIN[33], ~DIN[34], ~DIN[35], ~DIN[36], INT);  // AND_Gate
  S_R_Flip_Flop s_r_ff_1 (.Q(PWR), .reset(or_1_out), .preset(PWRON));  // open: S, R, clk, Qn
  or or_1 (or_1_out, and_2_out, PWROFF);
  or or_2 (RST, MRST, and_3_out);
  assign DOUT = {{15{1'b0}}, PWR};  // Bit_Extender bit_extender_1

  // Other names for the same wires on the sheet: WEN = DIN[0]; WADDR[15:0] = DIN[16:1]; WDATA[15:0] = DIN[32:17];
  //   INTCODE[3:0] = DIN[36:33]; INT_ASYNC = DIN[37]; CLK = DIN[38]
endmodule

module DeviceTTY (
  input  [38:0] DIN,
  output TTYCLK,
  output TTYEN,
  output TTYCLR,
  output [6:0] TTYASCII,
  output [15:0] DOUT
);

  wire and_2_out, and_5_out, and_7_out, INT, INT_PRINT, INT_RESET, nor_1_out, nor_2_out, not_1_out,
       register_3_q, s_r_ff_1_q, STOP;
  wire [7:0] adder_1_out, adder_2_out, adder_3_out, adder_4_out, multiplexer_1_out, multiplexer_2_out,
       multiplexer_3_out, register_1_q, register_2_q, register_4_q, register_5_q, subtractor_1_out;

  and and_1 (INT, DIN[37], DIN[38]);
  Adder adder_1 (.a(DIN[8:1]), .b(register_2_q), .out(adder_1_out));  // open: cin, cout
  Register register_1 (.D(adder_1_out), .en(DIN[0]), .clk(DIN[38]), .Q(register_1_q), .clr(INT_RESET));
  Register register_2 (.D(adder_2_out), .en(INT_PRINT), .clk(DIN[38]), .Q(register_2_q), .clr(INT_RESET));
  and and_2 (and_2_out, STOP, nor_1_out);
  Adder adder_2 (.a(8'h1), .b(register_1_q), .out(adder_2_out));  // open: cin, cout
  S_R_Flip_Flop s_r_ff_1 (.Q(s_r_ff_1_q), .reset(not_1_out), .preset(INT_PRINT));  // open: S, R, clk, Qn
  not not_1 (not_1_out, DIN[38]);
  Register #(.trigger("falling"), .width(1)) register_3 (
    .D(and_2_out), .en(1'b1), .clk(DIN[38]), .Q(register_3_q), .clr(INT_RESET));
  S_R_Flip_Flop s_r_ff_2 (.Q(TTYEN), .reset(register_3_q), .preset(INT_PRINT));  // open: S, R, clk, Qn
  and and_3 (INT_RESET, ~DIN[33], ~DIN[34], ~DIN[35], ~DIN[36], INT);  // AND_Gate
  and and_4 (INT_PRINT, DIN[33], ~DIN[34], ~DIN[35], ~DIN[36], DIN[37]);  // AND_Gate
  Multiplexer #(.width(8)) multiplexer_1 (
    .in0(register_5_q), .in1(adder_3_out), .out(multiplexer_1_out), .sel(s_r_ff_1_q));
  Adder adder_3 (.a(register_5_q), .b(8'h1), .out(adder_3_out));  // open: cin, cout
  RAM #(.dataWidth(16), .enables("line")) ram_1 (
    .addr(multiplexer_2_out), .we(DIN[0]), .clk(DIN[38]), .din(DIN[32:17]), .dout(DOUT));
  Multiplexer #(.width(8)) multiplexer_2 (
    .in0(adder_1_out), .in1(register_4_q), .out(multiplexer_2_out), .sel(DIN[38]));
  Subtractor subtractor_1 (.a(multiplexer_1_out), .b(8'h1), .out(subtractor_1_out));  // open: bin, bout
  and and_5 (and_5_out, STOP, ~and_7_out);  // AND_Gate
  Register #(.trigger("falling")) register_4 (
    .D(adder_4_out), .en(TTYEN), .clk(DIN[38]), .Q(register_4_q), .clr(INT_RESET));
  Register #(.trigger("falling")) register_5 (.D(multiplexer_3_out), .clk(DIN[38]), .Q(register_5_q));  // open: en, clr
  Multiplexer #(.width(8)) multiplexer_3 (
    .in0(multiplexer_1_out), .in1(subtractor_1_out), .out(multiplexer_3_out), .sel(and_5_out));
  Adder adder_4 (.a(8'h1), .b(register_4_q), .out(adder_4_out));  // open: cin, cout
  and and_6 (TTYCLR, ~DIN[33], DIN[34], ~DIN[35], ~DIN[36], INT);  // AND_Gate
  nor nor_1 (nor_1_out, register_5_q[1], register_5_q[2], register_5_q[3], register_5_q[4], register_5_q[5], register_5_q[6], register_5_q[7]);
  and and_7 (and_7_out, ~register_5_q[0], nor_1_out);  // AND_Gate
  nor nor_2 (nor_2_out, DOUT[0], DOUT[1], DOUT[2], DOUT[3], DOUT[4], DOUT[5], DOUT[6]);
  and and_8 (STOP, nor_2_out, DIN[38]);

  assign TTYASCII = DOUT[6:0];
  assign TTYCLK = DIN[38];

  // Other names for the same wires on the sheet: WEN = DIN[0]; WADDR[15:0] = DIN[16:1]; WDATA[15:0] = DIN[32:17];
  //   INTCODE[3:0] = DIN[36:33]; INT_ASYNC = DIN[37]; CLK = DIN[38]; EN = TTYEN; INT_CLEAR = TTYCLR
endmodule

module DeviceKeyboard (
  input  [38:0] DIN,
  input  KEYA,
  input  [6:0] KEYD,
  input  KEYCLK,
  input  KEYRST,
  output [15:0] DOUT
);

  wire INT;
  wire [7:0] adder_1_out, multiplexer_1_out, register_1_q;
  wire [15:0] bit_extender_1_out;

  and and_1 (INT, DIN[37], DIN[38]);
  Register #(.trigger("falling")) register_1 (
    .D(adder_1_out), .en(KEYA), .clk(DIN[38]), .Q(register_1_q), .clr(KEYRST));
  assign bit_extender_1_out = {{9{1'b0}}, KEYD};  // Bit_Extender bit_extender_1
  Multiplexer #(.width(8)) multiplexer_1 (.in0(DIN[8:1]), .in1(register_1_q), .out(multiplexer_1_out), .sel(DIN[38]));
  RAM #(.dataWidth(16), .enables("line"), .trigger("falling")) ram_1 (
    .addr(multiplexer_1_out), .we(1'b1), .clk(DIN[38]), .din(bit_extender_1_out), .dout(DOUT));
  and and_2 (KEYRST, ~DIN[33], ~DIN[34], ~DIN[35], ~DIN[36], INT);  // AND_Gate
  Adder adder_1 (.a(8'h1), .b(multiplexer_1_out), .out(adder_1_out));  // open: cin, cout

  assign KEYCLK = DIN[38];

  // Other names for the same wires on the sheet: WEN = DIN[0]; WADDR[15:0] = DIN[16:1]; WDATA[15:0] = DIN[32:17];
  //   INTCODE[3:0] = DIN[36:33]; INT_ASYNC = DIN[37]; CLK = DIN[38]; INT_RESET = KEYRST
endmodule
